// Logisim project Ch7.circ as structural Verilog
module main (
);

  wire Memory_p1, Memory_p2, Memory_p3, Registers_p1, Registers_p2, Registers_p4, undriven_3, undriven_4,
       undriven_7, undriven_8, undriven_9, undriven_11;
  wire [1:0] undriven_10;
  wire [15:0] n16_bit_alu_1_result, undriven, undriven_2, undriven_5, undriven_6;

  Instruction_Register Instruction_Register (.In(undriven), .Out(undriven_2), .Clock(undriven_3));
  Control_Logic Control_Logic ();
  _3_bit_register u_3_bit_register_1 (
    .Input(undriven_2[10:8]), .Clock(undriven_4), .Clock_2(undriven_7));  // open: Output
  _5_bit_register u_5_bit_register_1 (
    .Input(undriven_2[15:11]), .Clock(undriven_3), .Clock_2(undriven_4));  // open: Output
  _3_bit_register u_3_bit_register_2 (
    .Input(undriven_2[7:5]), .Clock(undriven_7), .Clock_2(undriven_8));  // open: Output
  _3_bit_register u_3_bit_register_3 (
    .Input(undriven_2[4:2]), .Clock(undriven_8), .Clock_2(undriven_9));  // open: Output
  _16_BIT_ALU u_16_bit_alu_1 (
    .A(undriven_5), .B(undriven_6), .Result(n16_bit_alu_1_result), .Operation(undriven_10));  // open: Invert_A, Invert_B, CarryOut_Overflow
  _8_bit_register u_8_bit_register_1 (
    .Input(undriven_2[7:0]), .Clock(undriven_9), .Clock_2(undriven_11));  // open: Output
  // _16_bit_8_word_register Registers: pin names not known; wires that end beside it: Registers_p1, Registers_p2, Registers_p2, Registers_p4, Registers_p4
  // _16_bit_8_word_register Memory: pin names not known; wires that end beside it: Memory_p1, Memory_p2, Memory_p3, Memory_p3
  Register_Note register_note_1 ();
endmodule

// 3
module _3_bit_register (
  input  Clock,
  input  [2:0] Input,
  input  Clock_2,
  output [2:0] Output
);

  D_Flip_Flop d_ff_1 (.clk(Clock), .D(Input[0]), .Q(Output[0]));  // open: Qn, preset, en, reset
  D_Flip_Flop d_ff_2 (.clk(Clock), .D(Input[1]), .Q(Output[1]));  // open: Qn, preset, en, reset
  D_Flip_Flop d_ff_3 (.clk(Clock), .D(Input[2]), .Q(Output[2]));  // open: Qn, preset, en, reset

  assign Clock_2 = Clock;
endmodule

// 5
module _5_bit_register (
  input  Clock,
  input  [4:0] Input,
  input  Clock_2,
  output [4:0] Output
);

  D_Flip_Flop d_ff_1 (.clk(Clock), .D(Input[0]), .Q(Output[0]));  // open: Qn, preset, en, reset
  D_Flip_Flop d_ff_2 (.clk(Clock), .D(Input[1]), .Q(Output[1]));  // open: Qn, preset, en, reset
  D_Flip_Flop d_ff_3 (.clk(Clock), .D(Input[2]), .Q(Output[2]));  // open: Qn, preset, en, reset
  D_Flip_Flop d_ff_4 (.clk(Clock), .D(Input[3]), .Q(Output[3]));  // open: Qn, preset, en, reset
  D_Flip_Flop d_ff_5 (.clk(Clock), .D(Input[4]), .Q(Output[4]));  // open: Qn, preset, en, reset

  assign Clock_2 = Clock;
endmodule

// 8
module _8_bit_register (
  input  Clock,
  input  [7:0] Input,
  input  Clock_2,
  output [7:0] Output
);

  D_Flip_Flop d_ff_1 (.clk(Clock), .D(Input[0]), .Q(Output[0]));  // open: Qn, preset, en, reset
  D_Flip_Flop d_ff_2 (.clk(Clock), .D(Input[1]), .Q(Output[1]));  // open: Qn, preset, en, reset
  D_Flip_Flop d_ff_3 (.clk(Clock), .D(Input[2]), .Q(Output[2]));  // open: Qn, preset, en, reset
  D_Flip_Flop d_ff_4 (.clk(Clock), .D(Input[3]), .Q(Output[3]));  // open: Qn, preset, en, reset
  D_Flip_Flop d_ff_5 (.clk(Clock), .D(Input[4]), .Q(Output[4]));  // open: Qn, preset, en, reset
  D_Flip_Flop d_ff_6 (.clk(Clock), .D(Input[5]), .Q(Output[5]));  // open: Qn, preset, en, reset
  D_Flip_Flop d_ff_7 (.clk(Clock), .D(Input[6]), .Q(Output[6]));  // open: Qn, preset, en, reset
  D_Flip_Flop d_ff_8 (.clk(Clock), .D(Input[7]), .Q(Output[7]));  // open: Qn, preset, en, reset

  assign Clock_2 = Clock;
endmodule

// 16
module _16_bit_register (
  input  Clock,
  input  [15:0] Input,
  input  Clock_2,
  output [15:0] Output
);

  D_Flip_Flop d_ff_1 (.clk(Clock), .D(Input[14]), .Q(Output[14]));  // open: Qn, preset, en, reset
  D_Flip_Flop d_ff_2 (.clk(Clock), .D(Input[6]), .Q(Output[6]));  // open: Qn, preset, en, reset
  D_Flip_Flop d_ff_3 (.clk(Clock), .D(Input[8]), .Q(Output[8]));  // open: Qn, preset, en, reset
  D_Flip_Flop d_ff_4 (.clk(Clock), .D(Input[10]), .Q(Output[10]));  // open: Qn, preset, en, reset
  D_Flip_Flop d_ff_5 (.clk(Clock), .D(Input[12]), .Q(Output[12]));  // open: Qn, preset, en, reset
  D_Flip_Flop d_ff_6 (.clk(Clock), .D(Input[13]), .Q(Output[13]));  // open: Qn, preset, en, reset
  D_Flip_Flop d_ff_7 (.clk(Clock), .D(Input[15]), .Q(Output[15]));  // open: Qn, preset, en, reset
  D_Flip_Flop d_ff_8 (.clk(Clock), .D(Input[0]), .Q(Output[0]));  // open: Qn, preset, en, reset
  D_Flip_Flop d_ff_9 (.clk(Clock), .D(Input[2]), .Q(Output[2]));  // open: Qn, preset, en, reset
  D_Flip_Flop d_ff_10 (.clk(Clock), .D(Input[4]), .Q(Output[4]));  // open: Qn, preset, en, reset
  D_Flip_Flop d_ff_11 (.clk(Clock), .D(Input[5]), .Q(Output[5]));  // open: Qn, preset, en, reset
  D_Flip_Flop d_ff_12 (.clk(Clock), .D(Input[7]), .Q(Output[7]));  // open: Qn, preset, en, reset
  D_Flip_Flop d_ff_13 (.clk(Clock), .D(Input[9]), .Q(Output[9]));  // open: Qn, preset, en, reset
  D_Flip_Flop d_ff_14 (.clk(Clock), .D(Input[11]), .Q(Output[11]));  // open: Qn, preset, en, reset
  D_Flip_Flop d_ff_15 (.clk(Clock), .D(Input[1]), .Q(Output[1]));  // open: Qn, preset, en, reset
  D_Flip_Flop d_ff_16 (.clk(Clock), .D(Input[3]), .Q(Output[3]));  // open: Qn, preset, en, reset

  assign Clock_2 = Clock;
endmodule

module Instruction_Register (
  input  [15:0] In,
  input  [15:0] Out,
  input  Clock
);
endmodule

module Splitter (
  input  [15:0] Instruction_Input,
  output [4:0] OpCode
);


  assign OpCode = Instruction_Input[15:11];
endmodule
